# Fritzing sketch BlockDetectormed_6_Dioder_Optokobler (saved by Fritzing 0.9.6b)
circuit board: 10.93cm x 5cm
breadboards: 1

parts:
  J1 = female pin header, 9 pins [form="♀ (female)"]
  J2 = female pin header, 9 pins [form="♀ (female)"]
  J3 = female pin header, 9 pins [form="♀ (female)"]  # not connected
  J4 = female pin header, 9 pins [form="♀ (female)"]  # not connected
  R9 = female pin header, 9 pins [form="♀ (female)"]
  R8 = Resistor [tolerance=±5% power=0.25 resistance=220 package=THT]
  R6 = Resistor [tolerance=±5% power=0.25 resistance=220 package=THT]
  R4 = Resistor [tolerance=±5% power=0.25 resistance=220 package=THT]
  R2 = Resistor [tolerance=±5% power=0.25 resistance=220 package=THT]
  R7 = Resistor [tolerance=±5% power=0.25 resistance=220 package=THT]
  R5 = Resistor [tolerance=±5% power=0.25 resistance=220 package=THT]
  R3 = Resistor [tolerance=±5% power=0.25 resistance=220 package=THT]
  R1 = Resistor [tolerance=±5% power=0.25 resistance=220 package=THT]
  J5 = female pin header, 9 pins [form="♀ (female)"]
  J6 = female pin header, 9 pins [form="♀ (female)"]
  IO4 = PCF8574N [part_number=TLP620 package="DIP16 [THT]"]
  IO3 = PCF8574N [package="DIP16 [THT]"]
  R12 = Resistor [tolerance=±5% power=0.25 resistance=220 package=THT]
  R17 = Resistor [tolerance=±5% power=0.25 resistance=220 package=THT]
  R10 = Resistor [tolerance=±5% power=0.25 resistance=220 package=THT]
  R16 = Resistor [tolerance=±5% power=0.25 resistance=220 package=THT]
  R13 = Resistor [tolerance=±5% power=0.25 resistance=220 package=THT]
  R11 = Resistor [tolerance=±5% power=0.25 resistance=220 package=THT]
  R14 = Resistor [tolerance=±5% power=0.25 resistance=220 package=THT]
  R15 = Resistor [tolerance=±5% power=0.25 resistance=220 package=THT]
  R18 = female pin header, 9 pins [form="♀ (female)"]
  IO2 = PCF8574N [package="DIP16 [THT]"]
  IO1 = PCF8574N [package="DIP16 [THT]"]

nets:
  N1: J1.pin1, J2.pin1, IO4.P4, IO4.P6, IO4.INT, IO4.SDA, IO3.P4, IO3.P6, IO3.INT, IO3.SDA, IO2.P4, IO2.P6, IO2.INT, IO2.SDA, IO1.P4, IO1.P6, IO1.INT, IO1.SDA
  N2: J1.pin2, IO1.P5
  N3: J1.pin3, IO2.P5
  N4: J1.pin4, IO1.P7
  N5: J1.pin5, IO2.P7
  N6: J1.pin6, IO1.SCL
  N7: J1.pin7, IO2.SCL
  N8: J1.pin8, IO1.VCC
  N9: J1.pin9, IO2.VCC
  N10: J2.pin2, IO3.P5
  N11: J2.pin3, IO4.P5
  N12: J2.pin4, IO3.P7
  N13: J2.pin5, IO4.P7
  N14: J2.pin6, IO3.SCL
  N15: J2.pin7, IO4.SCL
  N16: J2.pin8, IO3.VCC
  N17: J2.pin9, IO4.VCC
  GND: R9.pin1, J5.pin1, J6.pin1, IO4.A1, IO4.P0, IO4.P2, IO4.GND, IO3.A1, IO3.P0, IO3.P2, IO3.GND, R18.pin1, IO2.A1, IO2.P0, IO2.P2, IO2.GND, IO1.A1, IO1.P0, IO1.P2, IO1.GND
  N18: R9.pin2, R1.Pin_0, J5.pin2
  N19: R9.pin3, R2.Pin_0, J5.pin3
  N20: R9.pin4, R3.Pin_0, J5.pin4
  N21: R9.pin5, R4.Pin_0, J5.pin5
  N22: R9.pin6, R5.Pin_0, J5.pin6
  N23: R9.pin7, R6.Pin_0, J5.pin7
  N24: R9.pin8, R7.Pin_0, J5.pin8
  N25: R9.pin9, R8.Pin_0, J5.pin9
  N26: R8.Pin_1, IO2.A0
  N27: R6.Pin_1, IO2.A2
  N28: R4.Pin_1, IO2.P1
  N29: R2.Pin_1, IO2.P3
  N30: R7.Pin_1, IO1.A0
  N31: R5.Pin_1, IO1.A2
  N32: R3.Pin_1, IO1.P1
  N33: R1.Pin_1, IO1.P3
  N34: J6.pin2, R10.Pin_0, R18.pin2
  N35: J6.pin3, R11.Pin_0, R18.pin3
  N36: J6.pin4, R12.Pin_0, R18.pin4
  N37: J6.pin5, R13.Pin_0, R18.pin5
  N38: J6.pin6, R14.Pin_0, R18.pin6
  N39: J6.pin7, R15.Pin_0, R18.pin7
  N40: J6.pin8, R16.Pin_0, R18.pin8
  N41: J6.pin9, R17.Pin_0, R18.pin9
  N42: IO4.A0, R17.Pin_1
  N43: IO4.A2, R15.Pin_1
  N44: IO4.P1, R13.Pin_1
  N45: IO4.P3, R11.Pin_1
  N46: IO3.A0, R16.Pin_1
  N47: IO3.A2, R14.Pin_1
  N48: IO3.P1, R12.Pin_1
  N49: IO3.P3, R10.Pin_1

notes:
  Block Detector for 6 Dioder & Optokobler   OMJK1949

custom parts:
  PCF8574N: Remote 8-Bit I/O Expander for I 2C Bus
