# Fritzing sketch IHC_Replacment_001 (saved by Fritzing 0.9.6b)
circuit board: 14.98cm x 8.2cm
breadboards: 1

parts:
  IO1 = PCF8574N [package="DIP16 [THT]"]
  IO2 = ULN2803A [form="♂ (male)" package=THT]
  J2 = screw terminal, 9 pins
  J1 = Screw terminal - 2 pins [package=THT]
  DC1 = HW-613 [part_number=HW-613 package=THT]
  IO3 = PCF8574N [package="DIP16 [THT]"]
  IO4 = ULN2803A [form="♂ (male)" package=THT]
  J3 = screw terminal, 9 pins
  M1 = DOIT Esp32 DevKit v1 (30 pins long, 11 pins width) [part_number=ESP32S-PIN30]
  J4 = screw terminal, 9 pins
  J5 = screw terminal, 9 pins
  J6 = screw terminal, 9 pins
  J12 = female pin header, 2 pins [form="♀ (female)"]  # not connected
  J14 = female pin header, 9 pins [form="♀ (female)"]
  J13 = female pin header, 5 pins [form="♀ (female)"]  # not connected
  J11 = female pin header, 9 pins [form="♀ (female)"]
  Q1 = FQP27P06 [package=THT]  # not connected
  J15 = female pin header, 4 pins [form="♀ (female)"]
  J16 = female pin header, 4 pins [form="♀ (female)"]

nets:
  GND: IO1.A0, IO1.A1, IO1.A2, IO1.GND, IO2.pin9, IO3.GND, IO4.pin9, M1.GND, J14.pin9, J11.pin9, J15.pin2, J16.pin2
  N1: IO1.P0, IO2.pin1
  N2: IO1.P1, IO2.pin2
  N3: IO1.P2, IO2.pin3
  N4: IO1.P3, IO2.pin4
  N5: IO1.P4, IO2.pin5
  N6: IO1.P5, IO2.pin6
  N7: IO1.P6, IO2.pin7
  N8: IO1.P7, IO2.pin8
  SCL: IO1.SCL, IO3.SCL, M1.D22, J15.pin4, J16.pin4
  SDA: IO1.SDA, IO3.SDA, M1.D21, J15.pin1, J16.pin1
  3.3V: IO1.VCC, IO3.A0, IO3.A1, IO3.A2, IO3.VCC, M1.3V3, J15.pin3, J16.pin3
  N9: IO2.pin10, J2.pin9, J4.pin9, J5.pin9, J6.pin9
  N10: IO2.pin11, J2.pin8, J14.pin1
  N11: IO2.pin12, J2.pin7, J14.pin2
  N12: IO2.pin13, J2.pin6, J14.pin3
  N13: IO2.pin14, J2.pin5, J14.pin4
  N14: IO2.pin15, J2.pin4, J14.pin5
  N15: IO2.pin16, J2.pin3, J14.pin6
  N16: IO2.pin17, J2.pin2, J14.pin7
  N17: IO2.pin18, J2.pin1, J14.pin8
  N18: J1.pin1, DC1.pin2
  N19: IO3.P0, IO4.pin1
  N20: IO3.P1, IO4.pin2
  N21: IO3.P2, IO4.pin3
  N22: IO3.P3, IO4.pin4
  N23: IO3.P4, IO4.pin5
  N24: IO3.P5, IO4.pin6
  N25: IO3.P6, IO4.pin7
  N26: IO3.P7, IO4.pin8
  N27: IO4.pin10, J3.pin9
  N28: IO4.pin11, J3.pin8
  N29: IO4.pin12, J3.pin7
  N30: IO4.pin13, J3.pin6
  N31: IO4.pin14, J3.pin5
  N32: IO4.pin15, J3.pin4
  N33: IO4.pin16, J3.pin3
  N34: IO4.pin17, J3.pin2
  N35: IO4.pin18, J3.pin1

notes:
  SDA
  SCL
  3V3

custom parts:
  PCF8574N: Remote 8-Bit I/O Expander for I 2C Bus
  ULN2803A: Generic male header
  HW-613: DC-DC Converter, max 24V input
  DOIT Esp32 DevKit v1 (30 pins long, 11 pins width): The DOIT Esp32 DevKit v1 is one of the development board created by DOIT to evaluate the ESP-WROOM-32 module. It is based on the ESP32 microcontroller that boasts Wifi, Bluetooth, Ethernet and Low Power support all in a single chip. (vanepp) made breadboard work, adjusted pin numbering and labels and reduced size of schematic and cleaned up pcb. This chip is 30pins long (2 x15) and 11 pins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
  FQP27P06: Power Mosfet
